// Digital circuit 74-181.dig as structural Verilog
module _74_181 (
  input  A3,
  input  A2,
  input  A1,
  input  A0,
  input  B3,
  input  B2,
  input  B1,
  input  B0,
  input  S3,
  input  S2,
  input  S1,
  input  S0,
  input  M,
  input  Cn,
  output F0,
  output F1,
  output F2,
  output F3,
  output A_eq_B,
  output P,
  output Cn_plus_4,
  output G
);

  wire and_1_out, and_2_out, and_3_out, and_4_out, and_5_out, and_6_out, and_7_out, and_8_out, and_9_out,
       and_10_out, and_11_out, and_12_out, and_13_out, and_14_out, and_15_out, and_16_out, and_17_out,
       and_18_out, and_19_out, and_20_out, and_21_out, and_22_out, and_23_out, and_24_out, and_25_out,
       and_26_out, and_27_out, and_28_out, and_29_out, and_31_out, and_32_out, and_33_out, nand_1_out,
       nand_3_out, nor_1_out, nor_2_out, nor_3_out, nor_4_out, nor_5_out, nor_6_out, nor_7_out, nor_8_out,
       nor_9_out, nor_10_out, nor_11_out, nor_13_out, not_1_out, not_2_out, not_3_out, not_4_out, not_5_out,
       not_6_out, not_7_out, not_8_out, not_9_out;

  not not_1 (not_1_out, M);
  not not_2 (not_2_out, B0);
  not not_3 (not_3_out, B1);
  not not_4 (not_4_out, B2);
  not not_5 (not_5_out, B3);
  and and_1 (and_1_out, B3, S3, A3);
  and and_2 (and_2_out, not_5_out, S2, A3);
  and and_3 (and_3_out, not_5_out, S1);
  and and_4 (and_4_out, B3, S0);
  and and_5 (and_5_out, B2, S3, A2);
  and and_6 (and_6_out, not_4_out, S2, A2);
  and and_7 (and_7_out, not_4_out, S1);
  and and_8 (and_8_out, B2, S0);
  and and_9 (and_9_out, B1, S3, A1);
  and and_10 (and_10_out, not_3_out, S2, A1);
  and and_11 (and_11_out, not_3_out, S1);
  and and_12 (and_12_out, B1, S0);
  and and_13 (and_13_out, B0, S3, A0);
  and and_14 (and_14_out, not_2_out, S2, A0);
  and and_15 (and_15_out, not_2_out, S1);
  and and_16 (and_16_out, B0, S0);
  nor nor_1 (nor_1_out, and_1_out, and_2_out);
  nor nor_2 (nor_2_out, and_3_out, and_4_out, A3);
  nor nor_3 (nor_3_out, and_5_out, and_6_out);
  nor nor_4 (nor_4_out, and_7_out, and_8_out, A2);
  nor nor_5 (nor_5_out, and_9_out, and_10_out);
  nor nor_6 (nor_6_out, and_11_out, and_12_out, A1);
  nor nor_7 (nor_7_out, and_13_out, and_14_out);
  nor nor_8 (nor_8_out, and_15_out, and_16_out, A0);
  not not_6 (not_6_out, nor_2_out);
  not not_7 (not_7_out, nor_4_out);
  not not_8 (not_8_out, nor_6_out);
  not not_9 (not_9_out, nor_8_out);
  nand nand_1 (nand_1_out, not_1_out, Cn);
  xor xor_1 (F0, and_17_out, nand_1_out);
  and and_17 (and_17_out, nor_7_out, not_9_out);
  and and_18 (and_18_out, nor_8_out, not_1_out);
  and and_19 (and_19_out, Cn, nor_7_out, not_1_out);
  nor nor_9 (nor_9_out, and_19_out, and_18_out);
  xor xor_2 (F1, and_20_out, nor_9_out);
  and and_20 (and_20_out, nor_5_out, not_8_out);
  and and_21 (and_21_out, nor_6_out, not_1_out);
  and and_22 (and_22_out, nor_5_out, nor_8_out, not_1_out);
  nor nor_10 (nor_10_out, and_23_out, and_22_out, and_21_out);
  and and_23 (and_23_out, nor_5_out, nor_7_out, Cn, not_1_out);
  xor xor_3 (F2, and_24_out, nor_10_out);
  and and_24 (and_24_out, nor_3_out, not_7_out);
  and and_25 (and_25_out, not_7_out, not_1_out);
  and and_26 (and_26_out, nor_3_out, nor_6_out, not_1_out);
  nor nor_11 (nor_11_out, and_28_out, and_27_out, and_26_out, and_25_out);
  and and_27 (and_27_out, nor_3_out, nor_5_out, nor_8_out, not_1_out);
  and and_28 (and_28_out, nor_3_out, nor_5_out, nor_7_out, Cn, not_1_out);
  xor xor_4 (F3, and_29_out, nor_11_out);
  and and_29 (and_29_out, nor_1_out, not_6_out);
  and and_30 (A_eq_B, F3, F2, F1, F0);
  nand nand_2 (P, nor_1_out, nor_3_out, nor_5_out, nor_7_out);
  nand nand_3 (nand_3_out, nor_1_out, nor_3_out, nor_5_out, nor_7_out, Cn);
  and and_31 (and_31_out, nor_1_out, nor_3_out, nor_5_out, nor_8_out);
  nor nor_12 (Cn_plus_4, ~nor_13_out, ~nand_3_out);  // NOr
  and and_32 (and_32_out, nor_1_out, nor_3_out, nor_6_out);
  and and_33 (and_33_out, nor_1_out, nor_4_out);
  nor nor_13 (nor_13_out, nor_2_out, and_33_out, and_32_out, and_31_out);
  not not_10 (G, nor_13_out);
endmodule
