// Digital circuit ALU181.dig as structural Verilog
module ALU181 (
);

  wire _74181_1_pin1, _74181_1_pin2, _74181_1_pin3, _74181_1_pin4, _74181_1_pin5, _74181_1_pin6,
       _74181_1_pin7, _74181_1_pin8, _74181_1_pin9, _74181_1_pin10, _74181_1_pin11, _74181_1_pin12,
       _74181_2_pin1, _74181_2_pin2, _74181_2_pin7, _74181_2_pin9, _74181_2_pin10, _74181_2_pin11, A1_out,
       A2_out, A3_out, A5_out, A6_out, A7_out, B1_out, B2_out, B3_out, B5_out, B6_out, B7_out, undriven,
       undriven_2, undriven_3, undriven_4;

  LED Co (.in(undriven_4));
  LED F7 (.in(undriven_3));
  LED F5 (.in(_74181_1_pin10));
  LED F6 (.in(_74181_1_pin11));
  LED F3 (.in(undriven));
  LED F4 (.in(_74181_1_pin9));
  LED F1 (.in(_74181_2_pin10));
  LED F2 (.in(_74181_2_pin11));
  LED F0 (.in(_74181_2_pin9));
  _74181 _74181_1 (
    .pin1(_74181_1_pin1), .pin2(_74181_1_pin2), .pin3(_74181_1_pin3), .pin4(_74181_1_pin4),
    .pin5(_74181_1_pin5), .pin6(_74181_1_pin6), .pin7(_74181_1_pin7), .pin8(_74181_1_pin8),
    .pin9(_74181_1_pin9), .pin10(_74181_1_pin10), .pin11(_74181_1_pin11), .pin12(_74181_1_pin12));  // open: pin13, pin14, pin15, pin16, pin17, pin18, pin19, pin20, pin21, pin22, pin23, pin24
  DipSwitch S3 (.out(_74181_1_pin3));
  DipSwitch M (.out(_74181_1_pin8));
  DipSwitch S0 (.out(_74181_1_pin6));
  DipSwitch S1 (.out(_74181_1_pin5));
  DipSwitch S2 (.out(_74181_1_pin4));
  PowerSupply powersupply_1 (.VDD(undriven_2), .GND(_74181_1_pin12));
  _74181 _74181_2 (
    .pin1(_74181_2_pin1), .pin2(_74181_2_pin2), .pin3(_74181_1_pin3), .pin4(_74181_1_pin4),
    .pin5(_74181_1_pin5), .pin6(_74181_1_pin6), .pin7(_74181_2_pin7), .pin8(_74181_1_pin8),
    .pin9(_74181_2_pin9), .pin10(_74181_2_pin10), .pin11(_74181_2_pin11), .pin12(_74181_1_pin12));  // open: pin13, pin14, pin15, pin16, pin17, pin18, pin19, pin20, pin21, pin22, pin23, pin24
  DipSwitch B5 (.out(B5_out));
  DipSwitch B6 (.out(B6_out));
  DipSwitch B7 (.out(B7_out));
  DipSwitch B1 (.out(B1_out));
  DipSwitch B2 (.out(B2_out));
  DipSwitch B3 (.out(B3_out));
  DipSwitch B4 (.out(_74181_1_pin1));
  DipSwitch B0 (.out(_74181_2_pin1));
  DipSwitch A4 (.out(_74181_1_pin2));
  DipSwitch A5 (.out(A5_out));
  DipSwitch A6 (.out(A6_out));
  DipSwitch A7 (.out(A7_out));
  DipSwitch A0 (.out(_74181_2_pin2));
  DipSwitch A1 (.out(A1_out));
  DipSwitch A2 (.out(A2_out));
  DipSwitch A3 (.out(A3_out));
  DipSwitch Cn (.out(_74181_2_pin7));
endmodule
