// Digital circuit Memory Controller.dig as structural Verilog
module Memory_Controller (
  input  Control_MAR_In,
  input  Control_Clock,
  input  Control_Halt_In,
  input  User_Program,
  input  User_Inspect,
  input  User_Write,
  input  Control_RAM_In,
  input  Control_RAM_Out,
  output MAR_Clock,
  output Halt_Out,
  output RAM_Write,
  output RAM_Output_Enable,
  output User_Output_Enable,
  output Databus_Output_Enable,
  output Databus_Direction
);

  wire and_2_out, and_3_out, and_4_out, and_5_out, and_6_out, and_7_out, and_8_out, and_9_out, not_1_out,
       not_2_out, not_3_out, not_4_out, not_5_out, not_6_out, not_7_out;

  not not_1 (not_1_out, Control_MAR_In);
  not not_2 (not_2_out, Control_Clock);
  not not_3 (not_3_out, User_Program);
  not not_4 (not_4_out, User_Inspect);
  not not_5 (not_5_out, User_Write);
  not not_6 (not_6_out, Control_RAM_In);
  not not_7 (not_7_out, Control_RAM_Out);
  and and_1 (MAR_Clock, not_1_out, not_2_out);
  or or_1 (Halt_Out, not_3_out, Control_Halt_In);
  and and_2 (and_2_out, Control_RAM_In, User_Program);
  and and_3 (and_3_out, not_7_out, User_Program);
  and and_4 (and_4_out, not_3_out, not_5_out);
  and and_5 (and_5_out, not_3_out, User_Inspect);
  and and_6 (and_6_out, not_6_out, Control_RAM_Out, User_Program);
  and and_7 (and_7_out, not_3_out, not_4_out);
  or or_2 (User_Output_Enable, User_Program, User_Inspect);
  and and_8 (and_8_out, not_6_out, not_7_out);
  and and_9 (and_9_out, Control_RAM_In, Control_RAM_Out);
  and and_10 (Databus_Direction, Control_RAM_In, not_7_out, User_Program);
  or or_3 (RAM_Output_Enable, and_6_out, and_7_out);
  or or_4 (Databus_Output_Enable, and_8_out, and_9_out, not_3_out);
  or or_5 (RAM_Write, and_2_out, and_3_out, and_4_out, and_5_out);

  // Notes on the sheet:
  //   MAR_Clock: pin 19
  //   Halt_Out: pin 18
  //   RAM_Write: pin 13
  //   RAM_Output_Enable: pin 14
  //   User_Output_Enable: pin 15
  //   Databus_Output_Enable: pin 16
  //   Databus_Direction: pin 17
  //   Control_MAR_In: pin 4, default 1
  //   Control_Clock: pin 2
  //   Control_Halt_In: pin 3
  //   User_Program: pin 8, default 1
  //   User_Inspect: pin 7
  //   User_Write: pin 9
  //   Control_RAM_In: pin 5, default 1
  //   Control_RAM_Out: pin 6, default 1
endmodule
